# Fritzing sketch MotorController4 (saved by Fritzing 0.9.2b)
circuit board: 9.46575cm x 5.25349cm
stripboards: 1

parts:
  VIN = mystery part, 3 pins [chip_label=? part_number=Spade]
  GND = mystery part, 3 pins [chip_label=? part_number=Spade]
  V5 = Voltage Regulator - 5V [part_number=LM7805 package="TO220 [THT]"]
  C3 = Ceramic Capacitor [capacitance=100nF package="100 mil [THT, multilayer]"]
  R1 = Resistor [tolerance=±5% resistance=4.7k package=THT]
  R2 = Resistor [tolerance=±5% resistance=10k package=THT]
  R3 = Resistor [tolerance=±5% resistance=4.7k package=THT]
  R4 = Resistor [tolerance=±5% resistance=10k package=THT]
  R7 = Resistor [tolerance=±5% resistance=4.7k package=THT]
  R5 = Resistor [tolerance=±5% resistance=4.7 package=THT]
  R6 = Resistor [tolerance=±5% resistance=10k package=THT]
  R8 = Resistor [tolerance=±5% resistance=10k package=THT]
  RPWM = mystery part, 3 pins [chip_label=? part_number=Spade]
  LPWM = mystery part, 3 pins [chip_label=? part_number=Spade]
  LDIR = mystery part, 3 pins [chip_label=? part_number=Spade]
  C1 = Electrolytic Capacitor [capacitance=47µF package="100 mil [THT, electrolytic]"]
  ATmega328 = atmega328 [package=dip]
  C2 = Electrolytic Capacitor [capacitance=47µF package="100 mil [THT, electrolytic]"]
  I2C = mystery part, 6 pins [chip_label=? part_number="Connector Block"]
  RDIR = mystery part, 3 pins [chip_label=? part_number=Spade]
  Y1 = Resonator [frequency="16 Mhz" package=THT]
  R9 = Resistor [tolerance=±5% resistance=10k package=THT]
  Q4 = npn-Powertransistor [part_number=TIP142 package="TO220 [THT]"]
  Q2 = npn-Powertransistor [part_number=TIP142 package="TO220 [THT]"]
  Q1 = TRANSISTOR_NPN [part_number=2N3904 package=to-92-ammo]
  Q5 = TRANSISTOR_NPN [part_number=2N3904 package=to-92-ammo]
  LVCC = mystery part, 3 pins [chip_label=? part_number=Spade]
  RVCC = mystery part, 3 pins [chip_label=? part_number=Spade]
  D1 = BYV25X Diode [part_number=BYV25X package=THT]
  D2 = BYV25X Diode [part_number=BYV25X package=THT]

nets:
  N1: VIN.pin1, VIN.pin2, VIN.pin3, V5.input_voltage, C1.+, LVCC.pin1, LVCC.pin2, LVCC.pin3, RVCC.pin1, RVCC.pin2, RVCC.pin3, D1.k, D2.k
  GND: GND.pin1, GND.pin2, GND.pin3, V5.GND, C3.0, R2.Pin_1, R4.Pin_0, R6.Pin_1, R8.Pin_1, C1.-, ATmega328.GND, C2.-, I2C.pin4, Y1.GND, Q4.emitter, Q2.emitter, Q1.E, Q5.E
  N2: V5.output_voltage, C3.1, ATmega328.VCC, ATmega328.AVCC, ATmega328.AREF, C2.+, I2C.pin3, R9.Pin_1
  N3: R1.Pin_0, R2.Pin_0, Q1.B
  N4: R1.Pin_1, ATmega328.D13
  N5: R3.Pin_0, ATmega328.D5_(PWM)
  N6: R3.Pin_1, R4.Pin_1, Q2.base
  N7: R7.Pin_0, ATmega328.D6_(PWM)
  N8: R7.Pin_1, R8.Pin_0, Q4.base
  N9: R5.Pin_0, R6.Pin_0, Q5.B
  N10: R5.Pin_1, ATmega328.D12
  N11: RPWM.pin1, RPWM.pin2, RPWM.pin3, Q2.collector, D2.a
  N12: LPWM.pin1, LPWM.pin2, LPWM.pin3, Q4.collector, D1.a
  N13: LDIR.pin1, LDIR.pin2, LDIR.pin3, Q5.C
  N14: ATmega328.RESET, R9.Pin_0
  N15: ATmega328.D0_(RX), I2C.pin5
  N16: ATmega328.D1_(TX), I2C.pin6
  N17: ATmega328.XLAT1, Y1.0
  N18: ATmega328.XLAT2, Y1.pin_1
  N19: ATmega328.A4, I2C.pin2
  N20: ATmega328.A5, I2C.pin1
  N21: RDIR.pin1, RDIR.pin2, RDIR.pin3, Q1.C

notes:
  SCL
  SDA
  VCC
  GND
  RXD
  TXD
  Dual Motor Controller
  Version 4.3
  ©2015 That Ain't Working
  All Rights Reserved
  Dual Motor Controller (I2C), ©2015 That Ain't Working, All Rights Reserved, 4.3

custom parts:
  BYV25X Diode: BYV25X ultrafast rectifier diode 600V, 5-10A
