# Fritzing sketch MotorController6 (saved by Fritzing 0.9.2b)
circuit board: 6cm x 4.5cm
circuit board: 4.5cm x 4.5cm
breadboards: 1

parts:
  MSP430G2 = MSP430G2 [part_number=MSP420G2 package=THT]
  J1 = double row female pin header, 40 pins [form="♀ (female)"]
  RESET = Pushbutton [package="[THT]"]
  R1 = Resistor [tolerance=±5% resistance=10k package=THT]
  DIR = Screw terminal - 2 pins [package=THT]
  PWM = Screw terminal - 2 pins [package=THT]
  R2 = Resistor [tolerance=±5% resistance=4.7k package=THT]
  R3 = Resistor [tolerance=±5% resistance=4.7k package=THT]
  R4 = Resistor [tolerance=±5% resistance=4.7k package=THT]
  R5 = Resistor [tolerance=±5% resistance=4.7k package=THT]
  R6 = Resistor [tolerance=±5% resistance=10k package=THT]
  R7 = Resistor [tolerance=±5% resistance=10k package=THT]
  Q1 = pnp-Powertransistor [part_number=TIP142 package="TO220 [THT]"]
  Q2 = NPN-Transistor [part_number=LM3904 package="TO92 [THT]"]
  R8 = Resistor [tolerance=±5% resistance=220 package=THT]
  D1 = BYV25X Diode [package=THT]
  GND = male pin header, 3 pins [form="♂ (male)"]
  OUT = male pin header, 3 pins [form="♂ (male)"]
  IN = male pin header, 3 pins [form="♂ (male)"]
  COIL = male pin header, 3 pins [form="♂ (male)"]
  VIN = male pin header, 3 pins [form="♂ (male)"]
  J1_2 = male pin header, 2 pins [form="♂ (male)"]

nets:
  N1: MSP430G2.pin1, J1.pin1, R1.Pin_0
  N2: MSP430G2.pin3, J1.pin37
  N3: MSP430G2.pin4, J1.pin36
  N4: MSP430G2.pin7, R2.Pin_1
  N5: MSP430G2.pin8, R3.Pin_1
  N6: MSP430G2.pin9, R4.Pin_1
  N7: MSP430G2.pin10, R5.Pin_1
  N8: MSP430G2.pin14, J1.pin3
  N9: MSP430G2.pin15, J1.pin2
  N10: MSP430G2.pin16, RESET.Pin_1, RESET.Pin_2, R1.Pin_1
  N11: MSP430G2.pin20, J1.pin13, RESET.Pin_3, RESET.Pin_4, R6.Pin_1, R7.Pin_1
  N12: DIR.pin1, R2.Pin_0
  N13: DIR.pin2, R3.Pin_0
  N14: PWM.pin1, R4.Pin_0, R6.Pin_0
  N15: PWM.pin2, R5.Pin_0, R7.Pin_0
  N16: Q1.base, R8.Pin_0, J1_2.pin1
  N17: Q1.collector, D1.a, IN.pin1, IN.pin2, IN.pin3
  N18: Q1.emitter, Q2.E, R8.Pin_1, GND.pin1, GND.pin2, GND.pin3
  N19: Q2.B, J1_2.pin2
  N20: Q2.C, COIL.pin1, COIL.pin2, COIL.pin3
  N21: D1.k, OUT.pin1, OUT.pin2, OUT.pin3, VIN.pin1, VIN.pin2, VIN.pin3

notes:
  Motor
  PWM
  DIR

custom parts:
  MSP430G2: MSP430G2 Microcontroller by Texas Instruments. Off LunchPad
  BYV25X Diode: BYV25X ultrafast rectifier diode 600V, 5-10A
